// Logisim project ex5.circ as structural Verilog: 5 circuits, main circuit main
module main (
  input  [15:0] in_1,
  input  [3:0] in_2,
  output [15:0] out_3
);

  wire [15:0] multiplexer_1_out, multiplexer_2_out, multiplexer_3_out, Rot1_out_2, Rot2_out_2, Rot4_out_2,
       Rot8_out_2;

  RotRight1 Rot1 (.in_1(in_1), .out_2(Rot1_out_2));
  Multiplexer #(.enable("false"), .width(16)) multiplexer_1 (
    .in0(in_1), .in1(Rot1_out_2), .out(multiplexer_1_out), .sel(in_2[0]));
  Multiplexer #(.enable("false"), .width(16)) multiplexer_2 (
    .in0(multiplexer_1_out), .in1(Rot2_out_2), .out(multiplexer_2_out), .sel(in_2[1]));
  RotRight2 Rot2 (.in_1(multiplexer_1_out), .out_2(Rot2_out_2));
  RotRight4 Rot4 (.in_1(multiplexer_2_out), .out_2(Rot4_out_2));
  Multiplexer #(.enable("false"), .width(16)) multiplexer_3 (
    .in0(multiplexer_2_out), .in1(Rot4_out_2), .out(multiplexer_3_out), .sel(in_2[2]));
  RotRight8 Rot8 (.in_1(multiplexer_3_out), .out_2(Rot8_out_2));
  Multiplexer #(.enable("false"), .width(16)) multiplexer_4 (
    .in0(multiplexer_3_out), .in1(Rot8_out_2), .out(out_3), .sel(in_2[3]));
endmodule

module RotRight1 (
  input  [15:0] in_1,
  output [15:0] out_2
);


  assign out_2 = {in_1[0], in_1[15:1]};
endmodule

module RotRight2 (
  input  [15:0] in_1,
  output [15:0] out_2
);

  wire [15:0] Rot1_out_2;

  RotRight1 Rot1 (.in_1(in_1), .out_2(Rot1_out_2));
  RotRight1 Rot1second (.in_1(Rot1_out_2), .out_2(out_2));
endmodule

module RotRight4 (
  input  [15:0] in_1,
  output [15:0] out_2
);

  wire [15:0] Rot2_out_2;

  RotRight2 Rot2 (.in_1(in_1), .out_2(Rot2_out_2));
  RotRight2 Rot2second (.in_1(Rot2_out_2), .out_2(out_2));
endmodule

module RotRight8 (
  input  [15:0] in_1,
  output [15:0] out_2
);

  wire [15:0] Rot4_out_2;

  RotRight4 Rot4 (.in_1(in_1), .out_2(Rot4_out_2));
  RotRight4 Rot4second (.in_1(Rot4_out_2), .out_2(out_2));
endmodule
